// Logisim project LogicGates.circ as structural Verilog: 1 circuit, main circuit main
module main (
  input  Pin_1,
  input  Pin_1_2,
  input  Pin_2,
  input  Pin_1_3,
  input  in_5,
  input  in_6,
  input  Pin_2_2,
  input  A,
  input  A_2,
  input  B,
  input  B_2,
  input  in_12,
  input  in_13,
  input  in_14,
  input  in_15,
  input  in_16,
  input  in_17,
  input  in_18,
  input  in_19,
  input  in_20,
  input  in_21,
  input  in_22,
  input  in_23,
  input  A_3,
  input  B_3,
  input  C
);

  wire and_1_out, and_2_out, and_3_out, and_4_out, and_5_out, and_6_out, and_7_out, and_8_out, and_9_out,
       and_10_out, and_11_out, and_12_out, and_13_out, and_14_out, and_15_out, and_16_out, and_17_out,
       not_1_out, not_2_out, not_3_out, not_4_out, not_5_out, not_6_out, not_7_out, not_8_out, not_9_out,
       not_10_out, not_11_out, not_12_out, not_13_out, not_14_out, not_15_out, not_16_out, not_17_out,
       or_1_out, or_2_out, or_3_out, or_4_out, or_5_out, or_6_out, or_7_out, xnor_1_out, xnor_2_out,
       xor_1_out, xor_2_out;

  not not_1 (not_1_out, A_3);
  not not_2 (not_2_out, C);
  not not_3 (not_3_out, B_3);
  and and_1 (and_1_out, Pin_1, Pin_2);
  LED led_1 (.in(and_1_out));
  xor xor_1 (xor_1_out, Pin_1_3, Pin_2_2);
  LED led_2 (.in(xor_1_out));
  xnor xnor_1 (xnor_1_out, A, B_2);
  LED led_3 (.in(xnor_1_out));
  NotExactlyOne xnor_2 (.out(xnor_2_out), .in0(in_15), .in1(in_16), .in2(in_17));
  LED led_4 (.in(xnor_2_out));
  ExactlyOne xor_2 (.out(xor_2_out), .in0(in_20), .in1(in_22), .in2(in_23));
  LED led_5 (.in(xor_2_out));
  and and_2 (and_2_out, not_3_out, not_1_out);
  and and_3 (and_3_out, B_3, A_3);
  and and_4 (and_4_out, and_2_out, not_2_out);
  and and_5 (and_5_out, C, and_3_out);
  not not_4 (not_4_out, in_5);
  not not_5 (not_5_out, in_6);
  not not_6 (not_6_out, B);
  not not_7 (not_7_out, A_2);
  not not_8 (not_8_out, in_12);
  not not_9 (not_9_out, in_13);
  not not_10 (not_10_out, in_19);
  not not_11 (not_11_out, in_18);
  or or_1 (or_1_out, and_4_out, and_5_out);
  LED led_6 (.in(or_1_out));
  not not_12 (not_12_out, Pin_1_2);
  and and_6 (and_6_out, in_6, not_4_out);
  and and_7 (and_7_out, not_5_out, in_5);
  and and_8 (and_8_out, not_6_out, not_7_out);
  and and_9 (and_9_out, A_2, B);
  and and_10 (and_10_out, in_13, not_8_out);
  and and_11 (and_11_out, not_9_out, in_12);
  and and_12 (and_12_out, not_10_out, not_11_out);
  and and_13 (and_13_out, in_19, in_18);
  LED led_7 (.in(not_12_out));
  or or_2 (or_2_out, and_6_out, and_7_out);
  LED led_8 (.in(or_2_out));
  or or_3 (or_3_out, and_8_out, and_9_out);
  LED led_9 (.in(or_3_out));
  or or_4 (or_4_out, and_10_out, and_11_out);
  not not_13 (not_13_out, in_14);
  not not_14 (not_14_out, or_4_out);
  or or_5 (or_5_out, and_12_out, and_13_out);
  and and_14 (and_14_out, or_4_out, not_13_out);
  and and_15 (and_15_out, not_14_out, in_14);
  not not_15 (not_15_out, in_21);
  and and_16 (and_16_out, not_15_out, not_16_out);
  not not_16 (not_16_out, or_5_out);
  and and_17 (and_17_out, or_5_out, in_21);
  or or_6 (or_6_out, and_14_out, and_15_out);
  not not_17 (not_17_out, or_6_out);
  LED led_10 (.in(not_17_out));
  or or_7 (or_7_out, and_16_out, and_17_out);
  LED led_11 (.in(or_7_out));

  // Notes on the sheet:
  //   AND
  //   XOR
  //   XNOR
  //   NOT
endmodule
